// Logisim project AddressMux.circ as structural Verilog: 1 circuit, main circuit Address_Multiplexer
module Address_Multiplexer (
  input  [4:0] STATE,
  input  [15:0] MAR_VALUE,
  input  [15:0] PC_VALUE,
  output [15:0] ADDRESS_BUS
);

  wire comparator_1_eq, comparator_2_eq, comparator_3_eq, comparator_4_eq, or_1_out;

  Comparator #(.width(5), .mode("unsigned")) comparator_1 (
    .a(STATE), .b(5'b01010), .eq(comparator_1_eq));  // open: gt, lt
  Comparator #(.width(5), .mode("unsigned")) comparator_2 (
    .a(STATE), .b(5'b01011), .eq(comparator_2_eq));  // open: gt, lt
  Comparator #(.width(5), .mode("unsigned")) comparator_3 (
    .a(STATE), .b(5'b01100), .eq(comparator_3_eq));  // open: gt, lt
  Comparator #(.width(5), .mode("unsigned")) comparator_4 (
    .a(STATE), .b(5'b01111), .eq(comparator_4_eq));  // open: gt, lt
  or or_1 (or_1_out, comparator_1_eq, comparator_2_eq, comparator_3_eq, comparator_4_eq);
  Multiplexer #(.width(16), .disabled(0), .enable("false")) multiplexer_1 (
    .in0(PC_VALUE), .in1(MAR_VALUE), .out(ADDRESS_BUS), .sel(or_1_out));
endmodule
