// Logisim project CPU.circ as structural Verilog: 1 circuit, main circuit main
module main (
  input  in_1,
  input  in_2,
  input  [7:0] External_Data_Bus,
  output Ram_Enable,
  output Rom_Enable,
  output Write,
  output Write_Bar,
  output [15:0] Address_Out,
  output [7:0] External_Data_Bus_Out
);

  wire D0, D1, D2, D3, D4, D5, D6, D7, D11, D12, D13, D14, D15, D17, D18, not_1_out;
  wire [2:0] D8, D9, D10, D23;
  wire [3:0] D16;
  wire [4:0] D20;
  wire [7:0] D19, D24;
  wire [15:0] address_multiplexer_1_address_bus, D21, D22, D26;

  not not_1 (not_1_out, in_2);
  Datapath_main main_1 (
    .gp_read(D14), .gp_write(D15), .Clock(in_1), .Reset(not_1_out), .alu_operation(D16),
    .alu_store_high(D13), .gp_input_select(D10), .alu_store_low(D12), .gp_output_select(D9), .latch_alu(D11),
    .gp_lu_output_select(D8), .pc_increment(D7), .pc_set(D6), .ir_set_high(D3), .jr_set_high(D5),
    .mar_set_high(D1), .ir_set_low(D2), .jr_set_low(D4), .mar_set_low(D0), .flags(D23),
    .data_bus_output(D19), .data_bus_input(D24), .pc_count(D22), .mar_value(D21), .ir_value(D26));
  State_Machine state_machine_1 (.out_4(D20), .in_1(D26), .in_2(in_1), .in_3(not_1_out));
  Address_Multiplexer address_multiplexer_1 (
    .STATE(D20), .MAR_VALUE(D21), .PC_VALUE(D22), .ADDRESS_BUS(address_multiplexer_1_address_bus));
  memory_io memory_io_1 (
    .Read_Memory(D17), .Write_Memory(D18), .Internal_Data_Bus(D19), .External_Data_Bus(External_Data_Bus),
    .Address_In(address_multiplexer_1_address_bus), .Ram_Enable(Ram_Enable), .Rom_Enable(Rom_Enable),
    .Write(Write), .Write_Bar(Write_Bar), .Address_Out(Address_Out), .Internal_Data_Path_Out(D24),
    .External_Data_Path(External_Data_Bus_Out));  // open: Enabled
  CU_TRANSLATOR_main main_2 (
    .in_1(D23), .in_2(D20), .in_3(D26), .alu_operation(D16), .gb_op_S(D9), .gb_alu_op_S(D8), .ir_load_h(D3),
    .ir_load_l(D2), .gb_read(D14), .gb_write(D15), .pc_set(D6), .pc_increment(D7), .mem_read(D17),
    .alu_store_h(D13), .alu_store_l(D12), .gb_ip_s(D10), .mem_write(D18), .latch_alu(D11), .jr_load_h(D5),
    .jr_load_l(D4), .mar_load_h(D1), .mar_load_l(D0));
endmodule
