// Logisim project CU_TRANSLATOR.circ as structural Verilog: 1 circuit, main circuit main
module main (
  input  [2:0] in_1,
  input  [4:0] in_2,
  input  [15:0] in_3,
  output [3:0] alu_operation,
  output [2:0] gb_ip_s,
  output [2:0] gb_op_S,
  output [2:0] gb_alu_op_S,
  output ir_load_h,
  output ir_load_l,
  output gb_read,
  output gb_write,
  output pc_set,
  output pc_increment,
  output mem_read,
  output mem_write,
  output latch_alu,
  output alu_store_h,
  output alu_store_l,
  output mar_load_h,
  output mar_load_l,
  output jr_load_h,
  output jr_load_l
);

  wire and_22_out, and_24_out, and_26_out, and_27_out, and_28_out, and_29_out, and_30_out, and_31_out,
       and_32_out, and_33_out, and_34_out, and_36_out, and_37_out, and_38_out, and_39_out, gb_add_f, LOAD,
       MOVE, MULTIPLY, not_1_out, not_2_out, not_3_out, or_3_out, S_ALU_IMM, S_ALU_OPERATION, S_COPY_REG,
       S_EX_JUMP, S_FETCH_ADDRESS1, S_FETCH_ADDRESS2, S_FETCH_ADDRESS3, S_FETCH_ADDRESS4, S_FETCH_IMM,
       S_FETCH_M, S_STOR_1, S_STOR_2, S_STOR_M, S_TEMP_FETCH, S_TEMP_STORE;

  and and_1 (S_STOR_2, in_2[0], ~in_2[1], in_2[2], ~in_2[3], ~in_2[4]);  // AND_Gate
  and and_2 (S_ALU_IMM, ~in_2[0], ~in_2[1], in_2[2], ~in_2[3], in_2[4]);  // AND_Gate
  and and_3 (jr_load_l, in_2[0], ~in_2[1], ~in_2[2], ~in_2[3], in_2[4]);  // AND_Gate
  and and_4 (ir_load_h, in_2[0], ~in_2[1], ~in_2[2], ~in_2[3], ~in_2[4]);  // AND_Gate
  and and_5 (S_STOR_M, in_2[0], in_2[1], ~in_2[2], in_2[3], ~in_2[4]);  // AND_Gate
  and and_6 (S_STOR_1, ~in_2[0], ~in_2[1], in_2[2], ~in_2[3], ~in_2[4]);  // AND_Gate
  and and_7 (S_FETCH_ADDRESS1, ~in_2[0], ~in_2[1], ~in_2[2], in_2[3], ~in_2[4]);  // AND_Gate
  and and_8 (jr_load_h, ~in_2[0], ~in_2[1], ~in_2[2], ~in_2[3], in_2[4]);  // AND_Gate
  and and_9 (S_FETCH_ADDRESS2, in_2[0], ~in_2[1], ~in_2[2], in_2[3], ~in_2[4]);  // AND_Gate
  and and_10 (S_FETCH_ADDRESS4, ~in_2[0], in_2[1], in_2[2], in_2[3], ~in_2[4]);  // AND_Gate
  and and_11 (S_FETCH_ADDRESS3, in_2[0], ~in_2[1], in_2[2], in_2[3], ~in_2[4]);  // AND_Gate
  and and_12 (S_TEMP_FETCH, ~in_2[0], ~in_2[1], in_2[2], in_2[3], ~in_2[4]);  // AND_Gate
  and and_13 (ir_load_l, ~in_2[0], in_2[1], ~in_2[2], ~in_2[3], ~in_2[4]);  // AND_Gate
  and and_14 (S_EX_JUMP, ~in_2[0], in_2[1], ~in_2[2], ~in_2[3], in_2[4]);  // AND_Gate
  and and_15 (S_FETCH_M, ~in_2[0], in_2[1], ~in_2[2], in_2[3], ~in_2[4]);  // AND_Gate
  and and_16 (S_COPY_REG, in_2[0], in_2[1], in_2[2], ~in_2[3], ~in_2[4]);  // AND_Gate
  and and_17 (S_FETCH_IMM, ~in_2[0], in_2[1], in_2[2], ~in_2[3], ~in_2[4]);  // AND_Gate
  and and_18 (S_TEMP_STORE, in_2[0], in_2[1], in_2[2], in_2[3], ~in_2[4]);  // AND_Gate
  and and_19 (S_ALU_OPERATION, in_2[0], in_2[1], ~in_2[2], ~in_2[3], ~in_2[4]);  // AND_Gate
  and and_20 (MOVE, in_3[15], ~in_3[14], ~in_3[13], in_3[12], ~in_3[11]);  // AND_Gate
  assign gb_add_f = S_STOR_2 ? 1'b1 : 1'bz;  // Controlled_Buffer controlled_buffer_1
  and and_21 (LOAD, in_3[15], ~in_3[14], ~in_3[13], ~in_3[12], ~in_3[11]);  // AND_Gate
  not not_1 (not_1_out, S_STOR_2);
  assign gb_add_f = not_1_out ? 1'b0 : 1'bz;  // Controlled_Buffer controlled_buffer_2
  and and_22 (and_22_out, MULTIPLY, in_3[11], in_3[12], ~in_3[13], ~in_3[14], ~in_3[15]);  // AND_Gate
  assign gb_ip_s[0] = and_22_out ? gb_add_f : 1'bz;  // Controlled_Buffer controlled_buffer_3
  not not_2 (not_2_out, and_22_out);
  assign gb_ip_s[0] = not_2_out ? in_3[2] : 1'bz;  // Controlled_Buffer controlled_buffer_4
  and and_23 (MULTIPLY, ~in_3[15], ~in_3[14], ~in_3[13], in_3[12], in_3[11]);  // AND_Gate
  and and_24 (and_24_out, MULTIPLY, in_3[11], in_3[12], ~in_3[13], ~in_3[14], ~in_3[15]);  // AND_Gate
  and and_25 (alu_store_h, S_STOR_1, and_24_out);
  or or_1 (alu_store_l, S_TEMP_STORE, S_STOR_2, and_27_out);
  and and_26 (and_26_out, MULTIPLY, in_3[11], in_3[12], ~in_3[13], ~in_3[14], ~in_3[15]);  // AND_Gate
  and and_27 (and_27_out, S_STOR_1, ~and_26_out);  // AND_Gate
  and and_28 (and_28_out, in_1[0], and_29_out);
  or or_2 (pc_increment, jr_load_l, jr_load_h, S_FETCH_ADDRESS4, S_FETCH_ADDRESS3, S_FETCH_ADDRESS2, S_FETCH_ADDRESS1, S_ALU_IMM, S_FETCH_IMM, ir_load_l, ir_load_h);
  and and_29 (and_29_out, in_3[1], in_3[0]);
  assign alu_operation = and_32_out ? 4'b1100 : 4'bz;  // Controlled_Buffer controlled_buffer_5
  and and_30 (and_30_out, in_3[1], ~in_3[0]);  // AND_Gate
  and and_31 (and_31_out, in_1[2], and_30_out);
  or or_3 (or_3_out, and_28_out, and_31_out, and_34_out, and_37_out);
  and and_32 (and_32_out, MOVE, ~in_3[11], in_3[12], ~in_3[13], ~in_3[14], in_3[15]);  // AND_Gate
  not not_3 (not_3_out, and_32_out);
  assign alu_operation = not_3_out ? in_3[14:11] : 4'bz;  // Controlled_Buffer controlled_buffer_6
  or or_4 (gb_write, S_STOR_M, S_COPY_REG, and_36_out);
  and and_33 (and_33_out, ~in_3[1], in_3[0]);  // AND_Gate
  and and_34 (and_34_out, in_1[1], and_33_out);
  and and_35 (pc_set, or_3_out, S_EX_JUMP);
  and and_36 (and_36_out, ~in_3[10], ~in_3[9], S_ALU_OPERATION);  // AND_Gate
  and and_37 (and_37_out, ~in_3[1], ~in_3[0]);  // AND_Gate
  or or_5 (mem_read, jr_load_l, jr_load_h, S_FETCH_ADDRESS4, S_FETCH_ADDRESS3, S_FETCH_ADDRESS2, S_FETCH_ADDRESS1, S_ALU_IMM, S_FETCH_IMM, ir_load_l, ir_load_h, S_FETCH_M, S_TEMP_FETCH);
  or or_6 (gb_read, S_STOR_1, S_STOR_2, S_COPY_REG, S_FETCH_M, and_38_out);
  or or_7 (mem_write, S_STOR_M, S_TEMP_STORE);
  or or_8 (latch_alu, S_TEMP_FETCH, S_ALU_IMM, S_ALU_OPERATION);
  or or_9 (mar_load_h, S_FETCH_ADDRESS1, S_FETCH_ADDRESS3);
  or or_10 (mar_load_l, S_FETCH_ADDRESS4, S_FETCH_ADDRESS2);
  and and_38 (and_38_out, S_FETCH_IMM, and_39_out);
  and and_39 (and_39_out, in_3[15], ~in_3[14], ~in_3[13], ~in_3[12], ~in_3[11], LOAD);  // AND_Gate

  assign gb_alu_op_S = in_3[4:2];
  assign gb_ip_s[2:1] = in_3[4:3];
  assign gb_op_S = in_3[7:5];

  // Other names for the same wires on the sheet: _11 = in_3[11]; _12 = in_3[12]; _13 = in_3[13]; _14 = in_3[14];
  //   _2 = in_3[2]; _3 = in_3[3]; _4 = in_3[4]; _5 = in_3[5]; _6 = in_3[6]; _7 = in_3[7]; F0 = in_1[0]; F1 = in_1[1];
  //   F2 = in_1[2]; Q0 = in_2[0]; Q1 = in_2[1]; Q2 = in_2[2]; Q3 = in_2[3]; Q4 = in_2[4]; _0 = in_3[0]; _1 = in_3[1];
  //   _8 = in_3[8]; _9 = in_3[9]; _10 = in_3[10]; _15 = in_3[15]; S_FETCH1 = ir_load_h; S_FETCH2 = ir_load_l;
  //   S_LOAD_JUMP1 = jr_load_h; S_LOAD_JUMP2 = jr_load_l
endmodule
