// Logisim project Datapath.circ as structural Verilog
module main (
  input  mar_set_high,
  input  mar_set_low,
  input  [2:0] gp_input_select,
  input  [2:0] gp_output_select,
  input  [2:0] gp_lu_output_select,
  input  gp_read,
  input  gp_write,
  input  Clock,
  input  ir_set_high,
  input  ir_set_low,
  input  Reset,
  input  [3:0] alu_operation,
  input  jr_set_high,
  input  jr_set_low,
  input  alu_store_high,
  input  alu_store_low,
  input  latch_alu,
  input  pc_increment,
  input  pc_set,
  input  [7:0] data_bus_input,
  output [15:0] mar_value,
  output [15:0] ir_value,
  output [15:0] pc_count,
  output [7:0] data_bus_output,
  output [2:0] flags
);

  wire latch_store;
  wire [2:0] alu_1_cf;
  wire [7:0] alu_latch_output, general_purpose_register_1_alu_output_value, gp_data_bus_input;
  wire [15:0] alu_1_result, Jump_Register_out_6;

  or or_1 (latch_store, alu_store_high, alu_store_low);
  alu_latch alu_latch_1 (
    .clk(Clock), .store_hight(alu_store_high), .store_low(alu_store_low), .reset(Reset), .grap(latch_alu),
    .in_6(alu_1_result), .flags(alu_1_cf), .out(alu_latch_output), .flags_out(flags));
  ALU alu_1 (
    .Result(alu_1_result), .OP1(general_purpose_register_1_alu_output_value), .OP2(data_bus_output),
    .selector(alu_operation), .ZF(alu_1_cf[1]), .NF(alu_1_cf[2]), .CF(alu_1_cf[0]));
  General_purpose_Register general_purpose_register_1 (
    .Databus_output(gp_data_bus_input), .Databus_input(data_bus_output),
    .alu_output_value(general_purpose_register_1_alu_output_value), .write_data(gp_write),
    .read_data(gp_read), .InputSelect(gp_input_select), .Reset(Reset), .OutputSelect(gp_output_select),
    .AluOutputSelect(gp_lu_output_select), .Clock(Clock));
  Generic_16_bit_Register Memory_Address_Register (
    .out_6(mar_value), .SetLow(mar_set_low), .SetHigh(mar_set_high), .halfValueIn(data_bus_output),
    .Clock(Clock), .Reset(Reset));
  Generic_16_bit_Register Instruction_Register (
    .out_6(ir_value), .SetLow(ir_set_low), .SetHigh(ir_set_high), .halfValueIn(data_bus_output),
    .Clock(Clock), .Reset(Reset));
  Generic_16_bit_Register Jump_Register (
    .out_6(Jump_Register_out_6), .SetLow(jr_set_low), .SetHigh(jr_set_high), .halfValueIn(data_bus_output),
    .Clock(Clock), .Reset(Reset));
  PC_Register_main main_1 (
    .out_6(pc_count), .Increment(pc_increment), .newCount(Jump_Register_out_6), .Set(pc_set), .Reset(Reset),
    .in_5(Clock));
  Multiplexer #(.select(2), .width(8)) multiplexer_1 (
    .in0(data_bus_input), .in1(gp_data_bus_input), .in2(alu_latch_output), .in3(alu_latch_output),
    .out(data_bus_output), .sel({latch_store, gp_write}));  // open: en

  // Other names for the same wires on the sheet: databus_output[7:0] = data_bus_output
endmodule

module Generic_16_bit_Register (
  input  SetLow,
  input  SetHigh,
  input  [7:0] halfValueIn,
  input  Clock,
  input  Reset,
  output [15:0] out_6
);

  wire [7:0] controlled_buffer_1_out, controlled_buffer_2_out;

  assign controlled_buffer_1_out = SetHigh ? halfValueIn : 8'bz;  // Controlled_Buffer controlled_buffer_1
  assign controlled_buffer_2_out = SetLow ? halfValueIn : 8'bz;  // Controlled_Buffer controlled_buffer_2
  Register RegisterHigh (.D(controlled_buffer_1_out), .Q(out_6[15:8]), .clk(Clock), .clr(Reset));  // open: en
  Register registerLow (.D(controlled_buffer_2_out), .Q(out_6[7:0]), .clk(Clock), .clr(Reset));  // open: en
endmodule

module PC_Register (
  input  Increment,
  input  Set,
  input  [15:0] newCount,
  input  Reset,
  input  in_5,
  output [15:0] out_6
);

  Counter #(.width(16), .max('hffff)) counter_1 (
    .load(Set), .D(newCount), .count(Increment), .Q(out_6), .clk(in_5), .clr(Reset));  // open: carry
endmodule

module General_purpose_Register (
  input  [7:0] Databus_input,
  input  write_data,
  input  read_data,
  input  [2:0] InputSelect,
  input  [2:0] OutputSelect,
  input  [2:0] AluOutputSelect,
  input  Clock,
  input  Reset,
  output [7:0] Databus_output,
  output [7:0] alu_output_value
);

  wire demultiplexer_2_out0, demultiplexer_2_out1, demultiplexer_2_out2, demultiplexer_2_out3,
       demultiplexer_2_out4, demultiplexer_2_out5, demultiplexer_2_out6, demultiplexer_2_out7;
  wire [7:0] controlled_buffer_2_out, demultiplexer_1_out0, demultiplexer_1_out1, demultiplexer_1_out2,
       demultiplexer_1_out3, demultiplexer_1_out4, demultiplexer_1_out5, demultiplexer_1_out6,
       demultiplexer_1_out7, multiplexer_1_out, register_1_q, register_2_q, register_3_q, register_4_q,
       register_5_q, register_6_q, register_7_q, register_8_q;

  assign Databus_output = write_data ? multiplexer_1_out : 8'bz;  // Controlled_Buffer controlled_buffer_1
  assign controlled_buffer_2_out = read_data ? Databus_input : 8'bz;  // Controlled_Buffer controlled_buffer_2
  Demultiplexer #(.select(3), .width(8)) demultiplexer_1 (
    .out0(demultiplexer_1_out0), .out1(demultiplexer_1_out1), .out2(demultiplexer_1_out2),
    .out3(demultiplexer_1_out3), .out4(demultiplexer_1_out4), .out5(demultiplexer_1_out5),
    .out6(demultiplexer_1_out6), .out7(demultiplexer_1_out7), .in(controlled_buffer_2_out), .sel(InputSelect));  // open: en
  Demultiplexer #(.select(3)) demultiplexer_2 (
    .out0(demultiplexer_2_out0), .out1(demultiplexer_2_out1), .out2(demultiplexer_2_out2),
    .out3(demultiplexer_2_out3), .out4(demultiplexer_2_out4), .out5(demultiplexer_2_out5),
    .out6(demultiplexer_2_out6), .out7(demultiplexer_2_out7), .in(read_data), .sel(InputSelect));  // open: en
  Register register_1 (.D(demultiplexer_1_out0), .en(demultiplexer_2_out0), .Q(register_1_q), .clk(Clock), .clr(Reset));
  Register register_2 (.D(demultiplexer_1_out1), .en(demultiplexer_2_out1), .Q(register_2_q), .clk(Clock), .clr(Reset));
  Register register_3 (.D(demultiplexer_1_out2), .en(demultiplexer_2_out2), .Q(register_3_q), .clk(Clock), .clr(Reset));
  Register register_4 (.D(demultiplexer_1_out3), .en(demultiplexer_2_out3), .Q(register_4_q), .clk(Clock), .clr(Reset));
  Register register_5 (.D(demultiplexer_1_out4), .en(demultiplexer_2_out4), .Q(register_5_q), .clk(Clock), .clr(Reset));
  Register register_6 (.D(demultiplexer_1_out5), .en(demultiplexer_2_out5), .Q(register_6_q), .clk(Clock), .clr(Reset));
  Register register_7 (.D(demultiplexer_1_out6), .en(demultiplexer_2_out6), .Q(register_7_q), .clk(Clock), .clr(Reset));
  Register register_8 (.D(demultiplexer_1_out7), .en(demultiplexer_2_out7), .Q(register_8_q), .clk(Clock), .clr(Reset));
  Multiplexer #(.select(3), .width(8)) multiplexer_1 (
    .in0(register_1_q), .in1(register_2_q), .in2(register_3_q), .in3(register_4_q), .in4(register_5_q),
    .in5(register_6_q), .in6(register_7_q), .in7(register_8_q), .out(multiplexer_1_out), .sel(OutputSelect));  // open: en
  Multiplexer #(.select(3), .width(8)) multiplexer_2 (
    .in0(register_1_q), .in1(register_2_q), .in2(register_3_q), .in3(register_4_q), .in4(register_5_q),
    .in5(register_6_q), .in6(register_7_q), .in7(register_8_q), .out(alu_output_value), .sel(AluOutputSelect));  // open: en
endmodule

module _8_bit_AND (
  input  [7:0] OP1,
  input  [7:0] OP2,
  output [15:0] Result
);

  and and_1 (Result[0], OP1[0], OP2[0]);
  and and_2 (Result[1], OP1[1], OP2[1]);
  and and_3 (Result[2], OP1[2], OP2[2]);
  and and_4 (Result[3], OP1[3], OP2[3]);
  and and_5 (Result[4], OP1[4], OP2[4]);
  and and_6 (Result[5], OP1[5], OP2[5]);
  and and_7 (Result[6], OP1[6], OP2[6]);
  and and_8 (Result[7], OP1[7], OP2[7]);

  assign Result[15:8] = {8{1'b0}};

  // Notes on the sheet:
  //   8-Bit AND
endmodule

// 8
module _8_bit_OR (
  input  [7:0] OP1,
  input  [7:0] OP2,
  output [15:0] Result
);

  or or_1 (Result[0], OP1[0], OP2[0]);
  or or_2 (Result[1], OP1[1], OP2[1]);
  or or_3 (Result[2], OP1[2], OP2[2]);
  or or_4 (Result[3], OP1[3], OP2[3]);
  or or_5 (Result[4], OP1[4], OP2[4]);
  or or_6 (Result[5], OP1[5], OP2[5]);
  or or_7 (Result[6], OP1[6], OP2[6]);
  or or_8 (Result[7], OP1[7], OP2[7]);

  assign Result[15:8] = {8{1'b0}};

  // Notes on the sheet:
  //   8-Bit OR
endmodule

// +
module _1_bit_FullAdder (
  input  Carry_In,
  input  A,
  input  B,
  output Result,
  output Carry_Out
);

  wire and_1_out, and_2_out, xor_1_out;

  and and_1 (and_1_out, A, B);
  xor xor_1 (xor_1_out, A, B);
  or or_1 (Carry_Out, and_1_out, and_2_out);
  and and_2 (and_2_out, Carry_In, xor_1_out);
  xor xor_2 (Result, Carry_In, xor_1_out);

  // Notes on the sheet:
  //   1-bit Full Adder
endmodule

module _8_bit_FullAdder (
  input  [7:0] A,
  input  [7:0] B,
  output [15:0] Result
);

  wire n1_bit_fulladder_1_carry_out, n1_bit_fulladder_2_carry_out, n1_bit_fulladder_3_carry_out,
       n1_bit_fulladder_4_carry_out, n1_bit_fulladder_5_carry_out, n1_bit_fulladder_6_carry_out,
       n1_bit_fulladder_7_carry_out;

  _1_bit_FullAdder u_1_bit_fulladder_1 (
    .A(A[0]), .B(B[0]), .Carry_In(1'b0), .Carry_Out(n1_bit_fulladder_1_carry_out), .Result(Result[0]));
  _1_bit_FullAdder u_1_bit_fulladder_2 (
    .A(A[1]), .B(B[1]), .Carry_In(n1_bit_fulladder_1_carry_out), .Carry_Out(n1_bit_fulladder_2_carry_out),
    .Result(Result[1]));
  _1_bit_FullAdder u_1_bit_fulladder_3 (
    .A(A[2]), .B(B[2]), .Carry_In(n1_bit_fulladder_2_carry_out), .Carry_Out(n1_bit_fulladder_3_carry_out),
    .Result(Result[2]));
  _1_bit_FullAdder u_1_bit_fulladder_4 (
    .A(A[3]), .B(B[3]), .Carry_In(n1_bit_fulladder_3_carry_out), .Carry_Out(n1_bit_fulladder_4_carry_out),
    .Result(Result[3]));
  _1_bit_FullAdder u_1_bit_fulladder_5 (
    .A(A[4]), .B(B[4]), .Carry_In(n1_bit_fulladder_4_carry_out), .Carry_Out(n1_bit_fulladder_5_carry_out),
    .Result(Result[4]));
  _1_bit_FullAdder u_1_bit_fulladder_6 (
    .A(A[5]), .B(B[5]), .Carry_In(n1_bit_fulladder_5_carry_out), .Carry_Out(n1_bit_fulladder_6_carry_out),
    .Result(Result[5]));
  _1_bit_FullAdder u_1_bit_fulladder_7 (
    .A(A[6]), .B(B[6]), .Carry_In(n1_bit_fulladder_6_carry_out), .Carry_Out(n1_bit_fulladder_7_carry_out),
    .Result(Result[6]));
  _1_bit_FullAdder u_1_bit_fulladder_8 (
    .A(A[7]), .B(B[7]), .Carry_In(n1_bit_fulladder_7_carry_out), .Carry_Out(Result[8]), .Result(Result[7]));

  assign Result[15:9] = {7{1'b0}};

  // Notes on the sheet:
  //   8-bit Adder
endmodule

module _8_bit_SUB (
  input  [7:0] OP1,
  input  [7:0] OP2,
  output [15:0] Result
);

  wire n1_bit_fulladder_1_carry_out, n1_bit_fulladder_2_carry_out, n1_bit_fulladder_3_carry_out,
       n1_bit_fulladder_4_carry_out, n1_bit_fulladder_5_carry_out, n1_bit_fulladder_6_carry_out,
       n1_bit_fulladder_7_carry_out, xor_1_out, xor_2_out, xor_3_out, xor_4_out, xor_5_out, xor_6_out,
       xor_7_out, xor_8_out;

  xor xor_1 (xor_1_out, 1'b1, OP2[0]);
  xor xor_2 (xor_2_out, 1'b1, OP2[1]);
  xor xor_3 (xor_3_out, 1'b1, OP2[2]);
  xor xor_4 (xor_4_out, 1'b1, OP2[3]);
  xor xor_5 (xor_5_out, 1'b1, OP2[4]);
  xor xor_6 (xor_6_out, 1'b1, OP2[5]);
  xor xor_7 (xor_7_out, 1'b1, OP2[6]);
  xor xor_8 (xor_8_out, 1'b1, OP2[7]);
  _1_bit_FullAdder u_1_bit_fulladder_1 (
    .A(OP1[0]), .B(xor_1_out), .Carry_In(1'b1), .Carry_Out(n1_bit_fulladder_1_carry_out), .Result(Result[0]));
  _1_bit_FullAdder u_1_bit_fulladder_2 (
    .A(OP1[1]), .B(xor_2_out), .Carry_In(n1_bit_fulladder_1_carry_out),
    .Carry_Out(n1_bit_fulladder_2_carry_out), .Result(Result[1]));
  _1_bit_FullAdder u_1_bit_fulladder_3 (
    .A(OP1[2]), .B(xor_3_out), .Carry_In(n1_bit_fulladder_2_carry_out),
    .Carry_Out(n1_bit_fulladder_3_carry_out), .Result(Result[2]));
  _1_bit_FullAdder u_1_bit_fulladder_4 (
    .A(OP1[3]), .B(xor_4_out), .Carry_In(n1_bit_fulladder_3_carry_out),
    .Carry_Out(n1_bit_fulladder_4_carry_out), .Result(Result[3]));
  _1_bit_FullAdder u_1_bit_fulladder_5 (
    .A(OP1[4]), .B(xor_5_out), .Carry_In(n1_bit_fulladder_4_carry_out),
    .Carry_Out(n1_bit_fulladder_5_carry_out), .Result(Result[4]));
  _1_bit_FullAdder u_1_bit_fulladder_6 (
    .A(OP1[5]), .B(xor_6_out), .Carry_In(n1_bit_fulladder_5_carry_out),
    .Carry_Out(n1_bit_fulladder_6_carry_out), .Result(Result[5]));
  _1_bit_FullAdder u_1_bit_fulladder_7 (
    .A(OP1[6]), .B(xor_7_out), .Carry_In(n1_bit_fulladder_6_carry_out),
    .Carry_Out(n1_bit_fulladder_7_carry_out), .Result(Result[6]));
  _1_bit_FullAdder u_1_bit_fulladder_8 (
    .A(OP1[7]), .B(xor_8_out), .Carry_In(n1_bit_fulladder_7_carry_out), .Carry_Out(Result[8]),
    .Result(Result[7]));

  assign Result[15:9] = {7{1'b0}};

  // Notes on the sheet:
  //   8 bit SUB
endmodule

module _8_bit_Shifter (
  input  [7:0] OP1,
  output [15:0] Result
);

  wire and_1_out, and_3_out, and_4_out, and_5_out, and_6_out, and_7_out, and_8_out, and_9_out, and_10_out,
       and_11_out, and_12_out, and_14_out, not_1_out;

  not not_1 (not_1_out, 1'b1);
  and and_1 (and_1_out, OP1[7], 1'b1);
  and and_2 (Result[7], not_1_out, OP1[6]);
  and and_3 (and_3_out, OP1[6], 1'b1);
  or or_1 (Result[6], and_1_out, and_4_out);
  and and_4 (and_4_out, not_1_out, OP1[5]);
  and and_5 (and_5_out, OP1[5], 1'b1);
  or or_2 (Result[5], and_3_out, and_6_out);
  and and_6 (and_6_out, not_1_out, OP1[4]);
  and and_7 (and_7_out, OP1[4], 1'b1);
  or or_3 (Result[4], and_5_out, and_8_out);
  and and_8 (and_8_out, not_1_out, OP1[3]);
  and and_9 (and_9_out, OP1[3], 1'b1);
  or or_4 (Result[3], and_7_out, and_10_out);
  and and_10 (and_10_out, not_1_out, OP1[2]);
  and and_11 (and_11_out, OP1[2], 1'b1);
  or or_5 (Result[2], and_9_out, and_12_out);
  and and_12 (and_12_out, not_1_out, OP1[1]);
  and and_13 (Result[0], OP1[1], 1'b1);
  or or_6 (Result[1], and_11_out, and_14_out);
  and and_14 (and_14_out, not_1_out, OP1[0]);

  assign Result[15:8] = {8{1'b0}};

  // Notes on the sheet:
  //   1-SL/0-SR
  //   8-bit Shifter
endmodule

module _4_bit_FullAdder (
  input  [3:0] A,
  input  [3:0] B,
  output [4:0] Result
);

  wire n1_bit_fulladder_1_carry_out, n1_bit_fulladder_2_carry_out, n1_bit_fulladder_3_carry_out;

  _1_bit_FullAdder u_1_bit_fulladder_1 (
    .A(A[0]), .B(B[0]), .Carry_In(1'b0), .Carry_Out(n1_bit_fulladder_1_carry_out), .Result(Result[0]));
  _1_bit_FullAdder u_1_bit_fulladder_2 (
    .A(A[1]), .B(B[1]), .Carry_In(n1_bit_fulladder_1_carry_out), .Carry_Out(n1_bit_fulladder_2_carry_out),
    .Result(Result[1]));
  _1_bit_FullAdder u_1_bit_fulladder_3 (
    .A(A[2]), .B(B[2]), .Carry_In(n1_bit_fulladder_2_carry_out), .Carry_Out(n1_bit_fulladder_3_carry_out),
    .Result(Result[2]));
  _1_bit_FullAdder u_1_bit_fulladder_4 (
    .A(A[3]), .B(B[3]), .Carry_In(n1_bit_fulladder_3_carry_out), .Carry_Out(Result[4]), .Result(Result[3]));

  // Notes on the sheet:
  //   4-bit Full Adder
  //   C-IN
endmodule

module _4_bit_Multiplier (
  input  [3:0] OP1,
  input  [3:0] OP2,
  output [7:0] Reult
);

  wire [2:0] and_15_out;
  wire [3:0] and_4_out, and_8_out, and_12_out, n4_bit_fulladder_2_result, n4_bit_fulladder_3_result;

  and and_1 (and_4_out[3], OP2[3], OP1[3]);
  and and_2 (and_4_out[2], OP2[3], OP1[2]);
  and and_3 (and_4_out[1], OP2[3], OP1[1]);
  and and_4 (and_4_out[0], OP2[3], OP1[0]);
  and and_5 (and_8_out[3], OP2[2], OP1[3]);
  _4_bit_FullAdder u_4_bit_fulladder_1 (.A(n4_bit_fulladder_2_result), .B(and_4_out), .Result(Reult[7:3]));
  and and_6 (and_8_out[1], OP2[2], OP1[1]);
  and and_7 (and_8_out[2], OP2[2], OP1[2]);
  and and_8 (and_8_out[0], OP2[2], OP1[0]);
  and and_9 (and_12_out[3], OP2[1], OP1[3]);
  and and_10 (and_12_out[2], OP2[1], OP1[2]);
  _4_bit_FullAdder u_4_bit_fulladder_2 (
    .A(n4_bit_fulladder_3_result), .B(and_8_out), .Result({n4_bit_fulladder_2_result, Reult[2]}));
  and and_11 (and_12_out[1], OP2[1], OP1[1]);
  and and_12 (and_12_out[0], OP2[1], OP1[0]);
  and and_13 (and_15_out[2], OP2[0], OP1[3]);
  _4_bit_FullAdder u_4_bit_fulladder_3 (
    .A({1'b0, and_15_out}), .B(and_12_out), .Result({n4_bit_fulladder_3_result, Reult[1]}));
  and and_14 (and_15_out[1], OP2[0], OP1[2]);
  and and_15 (and_15_out[0], OP2[0], OP1[1]);
  and and_16 (Reult[0], OP2[0], OP1[0]);

  // Notes on the sheet:
  //   4-bit FullAdder
  //   4-bit FullAdder
  //   4-bit FullAdder
  //   4-bit Multiplier
endmodule

module _8_bit_Multiplier (
  input  [7:0] OP1,
  input  [7:0] OP2,
  output [15:0] Result
);

  wire [4:0] n8_bit_fulladder_3_result;
  wire [7:0] n4_bit_multiplier_1_reult, n4_bit_multiplier_2_reult, n4_bit_multiplier_3_reult;
  wire [7:4] n4_bit_multiplier_4_reult;
  wire [15:0] n8_bit_fulladder_2_result;
  wire [15:8] n8_bit_fulladder_1_result, n8_bit_fulladder_3_result_2;

  _4_bit_Multiplier u_4_bit_multiplier_1 (.OP1(OP1[7:4]), .OP2(OP2[7:4]), .Reult(n4_bit_multiplier_1_reult));
  _4_bit_Multiplier u_4_bit_multiplier_2 (.OP1(OP1[7:4]), .OP2(OP2[3:0]), .Reult(n4_bit_multiplier_2_reult));
  _8_bit_FullAdder u_8_bit_fulladder_1 (
    .A({3'b000, n8_bit_fulladder_3_result}), .B(n4_bit_multiplier_1_reult),
    .Result({n8_bit_fulladder_1_result, Result[15:8]}));
  _4_bit_Multiplier u_4_bit_multiplier_3 (.OP1(OP1[3:0]), .OP2(OP2[7:4]), .Reult(n4_bit_multiplier_3_reult));
  _8_bit_FullAdder u_8_bit_fulladder_2 (
    .A(n4_bit_multiplier_3_reult), .B(n4_bit_multiplier_2_reult),
    .Result({n8_bit_fulladder_2_result[15:9], n8_bit_fulladder_3_result[4], n8_bit_fulladder_2_result[7:0]}));
  _4_bit_Multiplier u_4_bit_multiplier_4 (
    .OP1(OP1[3:0]), .OP2(OP2[3:0]), .Reult({n4_bit_multiplier_4_reult, Result[3:0]}));
  _8_bit_FullAdder u_8_bit_fulladder_3 (
    .A({4'b0000, n4_bit_multiplier_4_reult}), .B(n8_bit_fulladder_2_result[7:0]),
    .Result({n8_bit_fulladder_3_result_2, n8_bit_fulladder_3_result[3:0], Result[7:4]}));

  // Notes on the sheet:
  //   8-bit Multiplier
  //   4-bit Multiplier
  //   4-bit Multiplier
  //   8-bit Adder
  //   8-bit Adder
  //   4-bit Multiplier
  //   4-bit Multiplier
  //   8-bit Adder
endmodule

module ALU (
  input  [7:0] OP1,
  input  [7:0] OP2,
  input  [3:0] selector,
  output [15:0] Result,
  output NF,
  output CF,
  output ZF
);

  wire ADD, and_6_out, and_7_out, and_8_out, LSL, MUL, SUB;
  wire [1:1] T;
  wire [15:0] ADD_result, AND_result, LSL_result, MULT_result, OR_result, SUB_result;

  _8_bit_FullAdder u_ADD (.A(OP1), .B(OP2), .Result(ADD_result));
  _8_bit_Multiplier MULT (.OP1(OP1), .OP2(OP2), .Result(MULT_result));
  _8_bit_SUB u_SUB (.OP1(OP1), .OP2(OP2), .Result(SUB_result));
  _8_bit_AND AND (.OP1(OP1), .OP2(OP2), .Result(AND_result));
  _8_bit_OR OR (.OP1(OP1), .OP2(OP2), .Result(OR_result));
  _8_bit_Shifter u_LSL (.OP1(OP1), .Result(LSL_result));
  Multiplexer #(.select(4), .width(16)) multiplexer_1 (
    .in0({16{1'b0}}), .in1(ADD_result), .in2(SUB_result), .in3(MULT_result), .in4(AND_result),
    .in5(OR_result), .in6({16{1'b0}}), .in7(LSL_result), .in8({16{1'b0}}), .in9({16{1'b0}}),
    .in10({16{1'b0}}), .in11({16{1'b0}}), .in12({16{1'b0}}), .in13({16{1'b0}}), .in14({16{1'b0}}),
    .in15({16{1'b0}}), .out(Result), .sel(selector));  // open: en
  and and_2 (MUL, ~selector[3], ~selector[2], selector[1], selector[0]);  // AND_Gate
  and and_3 (SUB, ~selector[3], ~selector[2], selector[1], ~selector[0]);  // AND_Gate
  and and_4 (ADD, ~selector[3], ~selector[2], ~selector[1], selector[0]);  // AND_Gate
  or or_2 (T[1], SUB, ADD);
  and and_5 (LSL, ~selector[3], selector[2], selector[1], selector[0]);  // AND_Gate
  and and_6 (and_6_out, ~Result[15], ~Result[14], ~Result[13], ~Result[12], ~Result[11], ~Result[10], ~Result[9], ~Result[8]);  // AND_Gate
  and and_7 (and_7_out, and_6_out, and_8_out);
  and and_8 (and_8_out, ~Result[7], ~Result[6], ~Result[5], ~Result[4], ~Result[3], ~Result[2], ~Result[1], ~Result[0]);  // AND_Gate
  Multiplexer multiplexer_2 (.in0(and_8_out), .in1(and_7_out), .out(ZF), .sel(MUL));  // open: en
  Multiplexer multiplexer_3 (.in0(Result[7]), .in1(Result[15]), .out(NF), .sel(MUL));  // open: en
  Multiplexer #(.select(2)) multiplexer_4 (
    .in0(1'b0), .in1(OP1[7]), .in2(Result[8]), .out(CF), .sel({T[1], LSL}));  // open: in3, en

  // Other names for the same wires on the sheet: PR7 = OP1[7]; T[0] = LSL
endmodule

module alu_latch (
  input  clk,
  input  store_hight,
  input  store_low,
  input  reset,
  input  grap,
  input  [15:0] in_6,
  input  [2:0] flags,
  output [7:0] out,
  output [2:0] flags_out
);

  wire not_1_out, or_1_out, or_2_out;
  wire [15:0] register_1_q;

  Register #(.width(16)) register_1 (.D(in_6), .en(grap), .Q(register_1_q), .clk(clk), .clr(reset));
  Multiplexer #(.width(8)) multiplexer_1 (
    .in0(register_1_q[7:0]), .in1(register_1_q[15:8]), .out(out), .sel(or_1_out), .en(or_2_out));
  or or_1 (or_1_out, not_1_out, store_hight);
  not not_1 (not_1_out, store_low);
  or or_2 (or_2_out, store_low, store_hight);
  assign flags_out = grap ? flags : 3'bz;  // Controlled_Buffer controlled_buffer_1

  // Other names for the same wires on the sheet: alu_result[15:0] = in_6; st_high = store_hight; st_low = store_low

  // Notes on the sheet:
  //   flags_out: pull=up
  //   out: pull=up
  //   alu result
endmodule
