// Logisim project General-purpose Register Block.circ as structural Verilog: 2 circuits, main circuit main
module main (
);

  General_purpose_Register general_purpose_register_1 ();  // open: Databus_output, Databus_input, alu_output_value, write_data, read_data, InputSelect, Reset, OutputSelect, AluOutputSelect, Clock
endmodule

module General_purpose_Register (
  input  [7:0] Databus_input,
  input  write_data,
  input  read_data,
  input  [2:0] InputSelect,
  input  [2:0] OutputSelect,
  input  [2:0] AluOutputSelect,
  input  Clock,
  input  Reset,
  output [7:0] Databus_output,
  output [7:0] alu_output_value
);

  wire demultiplexer_2_out0, demultiplexer_2_out1, demultiplexer_2_out2, demultiplexer_2_out3,
       demultiplexer_2_out4, demultiplexer_2_out5, demultiplexer_2_out6, demultiplexer_2_out7;
  wire [7:0] controlled_buffer_2_out, demultiplexer_1_out0, demultiplexer_1_out1, demultiplexer_1_out2,
       demultiplexer_1_out3, demultiplexer_1_out4, demultiplexer_1_out5, demultiplexer_1_out6,
       demultiplexer_1_out7, multiplexer_1_out, register_1_q, register_2_q, register_3_q, register_4_q,
       register_5_q, register_6_q, register_7_q, register_8_q;

  assign Databus_output = write_data ? multiplexer_1_out : 8'bz;  // Controlled_Buffer controlled_buffer_1
  assign controlled_buffer_2_out = read_data ? Databus_input : 8'bz;  // Controlled_Buffer controlled_buffer_2
  Demultiplexer #(.select(3), .width(8)) demultiplexer_1 (
    .out0(demultiplexer_1_out0), .out1(demultiplexer_1_out1), .out2(demultiplexer_1_out2),
    .out3(demultiplexer_1_out3), .out4(demultiplexer_1_out4), .out5(demultiplexer_1_out5),
    .out6(demultiplexer_1_out6), .out7(demultiplexer_1_out7), .in(controlled_buffer_2_out), .sel(InputSelect));  // open: en
  Demultiplexer #(.select(3)) demultiplexer_2 (
    .out0(demultiplexer_2_out0), .out1(demultiplexer_2_out1), .out2(demultiplexer_2_out2),
    .out3(demultiplexer_2_out3), .out4(demultiplexer_2_out4), .out5(demultiplexer_2_out5),
    .out6(demultiplexer_2_out6), .out7(demultiplexer_2_out7), .in(read_data), .sel(InputSelect));  // open: en
  Register register_1 (.D(demultiplexer_1_out0), .en(demultiplexer_2_out0), .Q(register_1_q), .clk(Clock), .clr(Reset));
  Register register_2 (.D(demultiplexer_1_out1), .en(demultiplexer_2_out1), .Q(register_2_q), .clk(Clock), .clr(Reset));
  Register register_3 (.D(demultiplexer_1_out2), .en(demultiplexer_2_out2), .Q(register_3_q), .clk(Clock), .clr(Reset));
  Register register_4 (.D(demultiplexer_1_out3), .en(demultiplexer_2_out3), .Q(register_4_q), .clk(Clock), .clr(Reset));
  Register register_5 (.D(demultiplexer_1_out4), .en(demultiplexer_2_out4), .Q(register_5_q), .clk(Clock), .clr(Reset));
  Register register_6 (.D(demultiplexer_1_out5), .en(demultiplexer_2_out5), .Q(register_6_q), .clk(Clock), .clr(Reset));
  Register register_7 (.D(demultiplexer_1_out6), .en(demultiplexer_2_out6), .Q(register_7_q), .clk(Clock), .clr(Reset));
  Register register_8 (.D(demultiplexer_1_out7), .en(demultiplexer_2_out7), .Q(register_8_q), .clk(Clock), .clr(Reset));
  Multiplexer #(.select(3), .width(8)) multiplexer_1 (
    .in0(register_1_q), .in1(register_2_q), .in2(register_3_q), .in3(register_4_q), .in4(register_5_q),
    .in5(register_6_q), .in6(register_7_q), .in7(register_8_q), .out(multiplexer_1_out), .sel(OutputSelect));  // open: en
  Multiplexer #(.select(3), .width(8)) multiplexer_2 (
    .in0(register_1_q), .in1(register_2_q), .in2(register_3_q), .in3(register_4_q), .in4(register_5_q),
    .in5(register_6_q), .in6(register_7_q), .in7(register_8_q), .out(alu_output_value), .sel(AluOutputSelect));  // open: en
endmodule
