// Logisim project Generic 16-bit Register.circ as structural Verilog: 2 circuits, main circuit main
module main (
);

  Generic_16_bit_Register generic_16_bit_register_1 ();  // open: out_6, SetLow, SetHigh, halfValueIn, Clock, Reset
endmodule

module Generic_16_bit_Register (
  input  SetLow,
  input  SetHigh,
  input  [7:0] halfValueIn,
  input  Clock,
  input  Reset,
  output [15:0] out_6
);

  wire [7:0] controlled_buffer_1_out, controlled_buffer_2_out;

  assign controlled_buffer_1_out = SetHigh ? halfValueIn : 8'bz;  // Controlled_Buffer controlled_buffer_1
  assign controlled_buffer_2_out = SetLow ? halfValueIn : 8'bz;  // Controlled_Buffer controlled_buffer_2
  Register RegisterHigh (.D(controlled_buffer_1_out), .Q(out_6[15:8]), .clk(Clock), .clr(Reset));  // open: en
  Register registerLow (.D(controlled_buffer_2_out), .Q(out_6[7:0]), .clk(Clock), .clr(Reset));  // open: en
endmodule
