// Logisim project MEMORY_IO.circ as structural Verilog: 2 circuits, main circuit main
module main (
);

  memory_io memory_io_1 ();  // open: Read_Memory, Write_Memory, Internal_Data_Bus, External_Data_Bus, Address_In, Enabled, Ram_Enable, Rom_Enable, Write, Write_Bar, Address_Out, Internal_Data_Path_Out, External_Data_Path
endmodule

module memory_io (
  input  Read_Memory,
  input  Write_Memory,
  input  [7:0] Internal_Data_Bus,
  input  [7:0] External_Data_Bus,
  input  [15:0] Address_In,
  output Enabled,
  output Ram_Enable,
  output Rom_Enable,
  output Write,
  output Write_Bar,
  output [15:0] Address_Out,
  output [7:0] Internal_Data_Path_Out,
  output [7:0] External_Data_Path
);

  wire comparator_1_eq, comparator_2_eq;

  xor xor_1 (Enabled, Read_Memory, Write_Memory);
  Multiplexer #(.width(8), .disabled(0), .enable("false")) multiplexer_1 (
    .in0({8{1'b0}}), .in1(External_Data_Bus), .out(Internal_Data_Path_Out), .sel(Read_Memory));
  Multiplexer #(.width(8), .disabled(0), .enable("false")) multiplexer_2 (
    .in0({8{1'b0}}), .in1(Internal_Data_Bus), .out(External_Data_Path), .sel(Write_Memory));
  Comparator #(.width(3)) comparator_1 (.a(Address_In[15:13]), .b(3'b000), .eq(comparator_1_eq));  // open: gt, lt
  Comparator #(.width(3)) comparator_2 (.a(Address_In[15:13]), .b(3'b001), .eq(comparator_2_eq));  // open: gt, lt
  not not_1 (Rom_Enable, comparator_1_eq);
  not not_2 (Ram_Enable, comparator_2_eq);
  not not_3 (Write_Bar, Write_Memory);

  assign Address_Out = Address_In;
  assign Write = Write_Memory;
endmodule
