// Logisim project Main.circ as structural Verilog: 1 circuit, main circuit main
module main (
  input  in_1,
  input  in_2,
  input  [4:0] in_3
);

  wire clock, controlled_buffer_1_out, Load_Ram, main_1_write, ram_1_p5, ram_1_p8, ram_1_p9;
  wire [7:0] controlled_buffer_2_out, data, main_1_external_data_bus_out, ram_1_p6;
  wire [15:0] D0, main_1_address_out, ram_1_p7;

  Clock clock_1 (.out(clock));
  Counter #(.width(16), .max('hffff)) counter_1 (
    .Q(D0), .clk(controlled_buffer_1_out));  // open: load, D, count, carry, clr
  assign controlled_buffer_1_out = Load_Ram ? clock : 1'bz;  // Controlled_Buffer controlled_buffer_1
  not not_1 (Load_Ram, in_1);
  ROM #(.addrWidth(16)) rom_1 (.addr(D0), .data(data));  // open: sel
  assign controlled_buffer_2_out = Load_Ram ? data : 8'bz;  // Controlled_Buffer controlled_buffer_2
  // Probe on ram_1_p5
  assign controlled_buffer_2_out = in_1 ? main_1_external_data_bus_out : 8'bz;  // Controlled_Buffer controlled_buffer_3
  // RAM ram_1: pin names not known; wires that end beside it: clock, in_2, in_3, controlled_buffer_2_out, ram_1_p5, ram_1_p6, ram_1_p7, ram_1_p8, ram_1_p9, ram_1_p9
  CPU_main main_1 (
    .in_1(clock), .in_2(in_1), .Write(main_1_write), .Write_Bar(ram_1_p8), .External_Data_Bus(ram_1_p6),
    .Address_Out(main_1_address_out), .External_Data_Bus_Out(main_1_external_data_bus_out));  // open: Ram_Enable, Rom_Enable
  assign ram_1_p7 = Load_Ram ? D0 : 16'bz;  // Controlled_Buffer controlled_buffer_4
  or or_1 (ram_1_p9, main_1_write, Load_Ram);
  assign ram_1_p7 = in_1 ? main_1_address_out : 16'bz;  // Controlled_Buffer controlled_buffer_5

  // Other names for the same wires on the sheet: Run = in_1

  // Notes on the sheet:
  //   contents of rom_1 (hex, n*v repeats v):
  //   84 8 3 84 4 6 c 8 3 14 4 2 18 28 89 60 0 1e 30 c 82 10 0 1e 10 70 89 80 0 1f
endmodule
