// Logisim project PC Register.circ as structural Verilog: 2 circuits, main circuit main
module main (
  input  Increment,
  input  Set,
  input  [15:0] newCount,
  input  Reset,
  input  in_5,
  output [15:0] out_6
);

  Counter #(.width(16), .max('hffff)) counter_1 (
    .load(Set), .D(newCount), .count(Increment), .Q(out_6), .clk(in_5), .clr(Reset));  // open: carry
endmodule

module try (
  input  [15:0] in_1,
  input  in_2,
  input  in_3,
  input  in_4,
  output [15:0] out_5
);

  wire clock_1_out;

  Clock clock_1 (.out(clock_1_out));
  main main_1 (.out_6(out_5), .Increment(in_3), .newCount(in_1), .Set(in_2), .Reset(in_4), .in_5(clock_1_out));
endmodule
