// Logisim project RAM.circ as structural Verilog: 2 circuits, main circuit main
module main (
);

  RAM ram_1 ();  // open: Read_data, Write_data, Clock, Reset, Read, Write, OutputSelect, RAM_output, Copy_To, Copy_From, InputSelect
endmodule

module RAM (
  input  [7:0] Write_data,
  input  Read,
  input  Write,
  input  [15:0] InputSelect,
  input  [4:0] OutputSelect,
  input  Clock,
  input  Reset,
  input  [4:0] Copy_From,
  input  [4:0] Copy_To,
  output [7:0] Read_data,
  output [7:0] RAM_output
);

  wire _0, _1, _2, _3, _4, _5, _6, _7, _8, _9, _10, _11, _12, _13, _14, _15, _16, _17, _18, _19, _20, _21,
       _22, _23, _24, _25, _26, _27, _28, _29, _30, _31, y;
  wire [4:0] multiplexer_2_out, multiplexer_3_out;
  wire [7:0] controlled_buffer_2_out, D0, D1, D2, D3, D4, D5, D6, D7, D8, D9, D10, D11, D12, D13, D14, D15,
       D16, D17, D18, D19, D20, D21, D22, D23, D24, D25, D26, D27, D28, D29, D30, D31, demultiplexer_1_out0,
       demultiplexer_1_out1, demultiplexer_1_out2, demultiplexer_1_out3, demultiplexer_1_out4,
       demultiplexer_1_out5, demultiplexer_1_out6, demultiplexer_1_out7, demultiplexer_1_out8,
       demultiplexer_1_out9, demultiplexer_1_out10, demultiplexer_1_out11, demultiplexer_1_out12,
       demultiplexer_1_out13, demultiplexer_1_out14, demultiplexer_1_out15, demultiplexer_1_out16,
       demultiplexer_1_out17, demultiplexer_1_out18, demultiplexer_1_out19, demultiplexer_1_out20,
       demultiplexer_1_out21, demultiplexer_1_out22, demultiplexer_1_out23, demultiplexer_1_out24,
       demultiplexer_1_out25, demultiplexer_1_out26, demultiplexer_1_out27, demultiplexer_1_out28,
       demultiplexer_1_out29, demultiplexer_1_out30, demultiplexer_1_out31, multiplexer_1_out,
       multiplexer_4_out, O0, O1, O2, O3, O4, O5, O6, O7, O8, O9, O10, O11, O12, O13, O14, O15, O16, O17,
       O18, O19, O20, O21, O22, O23, O24, O25, O26, O27, O28, O29, O30, O31;

  Demultiplexer #(.select(5), .width(8)) demultiplexer_1 (
    .out0(demultiplexer_1_out0), .out1(demultiplexer_1_out1), .out2(demultiplexer_1_out2),
    .out3(demultiplexer_1_out3), .out4(demultiplexer_1_out4), .out5(demultiplexer_1_out5),
    .out6(demultiplexer_1_out6), .out7(demultiplexer_1_out7), .out8(demultiplexer_1_out8),
    .out9(demultiplexer_1_out9), .out10(demultiplexer_1_out10), .out11(demultiplexer_1_out11),
    .out12(demultiplexer_1_out12), .out13(demultiplexer_1_out13), .out14(demultiplexer_1_out14),
    .out15(demultiplexer_1_out15), .out16(demultiplexer_1_out16), .out17(demultiplexer_1_out17),
    .out18(demultiplexer_1_out18), .out19(demultiplexer_1_out19), .out20(demultiplexer_1_out20),
    .out21(demultiplexer_1_out21), .out22(demultiplexer_1_out22), .out23(demultiplexer_1_out23),
    .out24(demultiplexer_1_out24), .out25(demultiplexer_1_out25), .out26(demultiplexer_1_out26),
    .out27(demultiplexer_1_out27), .out28(demultiplexer_1_out28), .out29(demultiplexer_1_out29),
    .out30(demultiplexer_1_out30), .out31(demultiplexer_1_out31), .in(multiplexer_1_out), .sel(Copy_To));  // open: en
  Multiplexer #(.select(5), .width(8)) multiplexer_1 (
    .in0(O0), .in1(O1), .in2(O2), .in3(O3), .in4(O4), .in5(O5), .in6(O6), .in7(O7), .in8(O8), .in9(O9),
    .in10(O10), .in11(O11), .in12(O12), .in13(O13), .in14(O14), .in15(O15), .in16(O16), .in17(O17),
    .in18(O18), .in19(O19), .in20(O20), .in21(O21), .in22(O22), .in23(O23), .in24(O24), .in25(O25),
    .in26(O26), .in27(O27), .in28(O28), .in29(O29), .in30(O30), .in31(O31), .out(multiplexer_1_out),
    .sel(Copy_From));  // open: en
  assign Read_data = Read ? multiplexer_4_out : 8'bz;  // Controlled_Buffer controlled_buffer_1
  assign controlled_buffer_2_out = Write ? Write_data : 8'bz;  // Controlled_Buffer controlled_buffer_2
  not not_1 (y, Write);
  assign D30 = y ? demultiplexer_1_out30 : 8'bz;  // Controlled_Buffer controlled_buffer_3
  assign D31 = y ? demultiplexer_1_out31 : 8'bz;  // Controlled_Buffer controlled_buffer_4
  Demultiplexer #(.select(5), .width(8)) demultiplexer_2 (
    .out0(D0), .out1(D1), .out2(D2), .out3(D3), .out4(D4), .out5(D5), .out6(D6), .out7(D7), .out8(D8),
    .out9(D9), .out10(D10), .out11(D11), .out12(D12), .out13(D13), .out14(D14), .out15(D15), .out16(D16),
    .out17(D17), .out18(D18), .out19(D19), .out20(D20), .out21(D21), .out22(D22), .out23(D23), .out24(D24),
    .out25(D25), .out26(D26), .out27(D27), .out28(D28), .out29(D29), .out30(D30), .out31(D31),
    .in(controlled_buffer_2_out), .sel(multiplexer_2_out));  // open: en
  Multiplexer #(.width(5)) multiplexer_2 (
    .in0(InputSelect[4:0]), .in1(Copy_To), .out(multiplexer_2_out), .sel(y));  // open: en
  Demultiplexer #(.select(5)) demultiplexer_3 (
    .out0(_0), .out1(_1), .out2(_2), .out3(_3), .out4(_4), .out5(_5), .out6(_6), .out7(_7), .out8(_8),
    .out9(_9), .out10(_10), .out11(_11), .out12(_12), .out13(_13), .out14(_14), .out15(_15), .out16(_16),
    .out17(_17), .out18(_18), .out19(_19), .out20(_20), .out21(_21), .out22(_22), .out23(_23), .out24(_24),
    .out25(_25), .out26(_26), .out27(_27), .out28(_28), .out29(_29), .out30(_30), .out31(_31), .in(1'b1),
    .sel(multiplexer_3_out));  // open: en
  Multiplexer #(.width(5)) multiplexer_3 (
    .in0(InputSelect[4:0]), .in1(Copy_To), .out(multiplexer_3_out), .sel(y));  // open: en
  assign D28 = y ? demultiplexer_1_out28 : 8'bz;  // Controlled_Buffer controlled_buffer_5
  assign D29 = y ? demultiplexer_1_out29 : 8'bz;  // Controlled_Buffer controlled_buffer_6
  assign D27 = y ? demultiplexer_1_out27 : 8'bz;  // Controlled_Buffer controlled_buffer_7
  assign D25 = y ? demultiplexer_1_out25 : 8'bz;  // Controlled_Buffer controlled_buffer_8
  assign D26 = y ? demultiplexer_1_out26 : 8'bz;  // Controlled_Buffer controlled_buffer_9
  assign D24 = y ? demultiplexer_1_out24 : 8'bz;  // Controlled_Buffer controlled_buffer_10
  Register register_1 (.D(D0), .en(_0), .Q(O0), .clk(Clock), .clr(Reset));
  Register register_2 (.D(D1), .en(_1), .Q(O1), .clk(Clock), .clr(Reset));
  Register register_3 (.D(D2), .en(_2), .Q(O2), .clk(Clock), .clr(Reset));
  Register register_4 (.D(D3), .en(_3), .Q(O3), .clk(Clock), .clr(Reset));
  Register register_5 (.D(D4), .en(_4), .Q(O4), .clk(Clock), .clr(Reset));
  Register register_6 (.D(D5), .en(_5), .Q(O5), .clk(Clock), .clr(Reset));
  Register register_7 (.D(D6), .en(_6), .Q(O6), .clk(Clock), .clr(Reset));
  Register register_8 (.D(D7), .en(_7), .Q(O7), .clk(Clock), .clr(Reset));
  assign D22 = y ? demultiplexer_1_out22 : 8'bz;  // Controlled_Buffer controlled_buffer_11
  assign D23 = y ? demultiplexer_1_out23 : 8'bz;  // Controlled_Buffer controlled_buffer_12
  assign D20 = y ? demultiplexer_1_out20 : 8'bz;  // Controlled_Buffer controlled_buffer_13
  assign D21 = y ? demultiplexer_1_out21 : 8'bz;  // Controlled_Buffer controlled_buffer_14
  Register register_9 (.D(D8), .en(_8), .Q(O8), .clk(Clock), .clr(Reset));
  Register register_10 (.D(D9), .en(_9), .Q(O9), .clk(Clock), .clr(Reset));
  Register register_11 (.D(D10), .en(_10), .Q(O10), .clk(Clock), .clr(Reset));
  Register register_12 (.D(D11), .en(_11), .Q(O11), .clk(Clock), .clr(Reset));
  Register register_13 (.D(D12), .en(_12), .Q(O12), .clk(Clock), .clr(Reset));
  Register register_14 (.D(D13), .en(_13), .Q(O13), .clk(Clock), .clr(Reset));
  Register register_15 (.D(D14), .en(_14), .Q(O14), .clk(Clock), .clr(Reset));
  Register register_16 (.D(D15), .en(_15), .Q(O15), .clk(Clock), .clr(Reset));
  assign D19 = y ? demultiplexer_1_out19 : 8'bz;  // Controlled_Buffer controlled_buffer_15
  assign D17 = y ? demultiplexer_1_out17 : 8'bz;  // Controlled_Buffer controlled_buffer_16
  assign D18 = y ? demultiplexer_1_out18 : 8'bz;  // Controlled_Buffer controlled_buffer_17
  Register register_17 (.D(D16), .en(_16), .Q(O16), .clk(Clock), .clr(Reset));
  Register register_18 (.D(D17), .en(_17), .Q(O17), .clk(Clock), .clr(Reset));
  Register register_19 (.D(D18), .en(_18), .Q(O18), .clk(Clock), .clr(Reset));
  Register register_20 (.D(D19), .en(_19), .Q(O19), .clk(Clock), .clr(Reset));
  Register register_21 (.D(D20), .en(_20), .Q(O20), .clk(Clock), .clr(Reset));
  Register register_22 (.D(D21), .en(_21), .Q(O21), .clk(Clock), .clr(Reset));
  Register register_23 (.D(D22), .en(_22), .Q(O22), .clk(Clock), .clr(Reset));
  Register register_24 (.D(D23), .en(_23), .Q(O23), .clk(Clock), .clr(Reset));
  assign D16 = y ? demultiplexer_1_out16 : 8'bz;  // Controlled_Buffer controlled_buffer_18
  Register register_25 (.D(D24), .en(_24), .Q(O24), .clk(Clock), .clr(Reset));
  Register register_26 (.D(D25), .en(_25), .Q(O25), .clk(Clock), .clr(Reset));
  Register register_27 (.D(D26), .en(_26), .Q(O26), .clk(Clock), .clr(Reset));
  Register register_28 (.D(D27), .en(_27), .Q(O27), .clk(Clock), .clr(Reset));
  Register register_29 (.D(D28), .en(_28), .Q(O28), .clk(Clock), .clr(Reset));
  Register register_30 (.D(D29), .en(_29), .Q(O29), .clk(Clock), .clr(Reset));
  Register register_31 (.D(D30), .en(_30), .Q(O30), .clk(Clock), .clr(Reset));
  Register register_32 (.D(D31), .en(_31), .Q(O31), .clk(Clock), .clr(Reset));
  assign D14 = y ? demultiplexer_1_out14 : 8'bz;  // Controlled_Buffer controlled_buffer_19
  assign D15 = y ? demultiplexer_1_out15 : 8'bz;  // Controlled_Buffer controlled_buffer_20
  assign D12 = y ? demultiplexer_1_out12 : 8'bz;  // Controlled_Buffer controlled_buffer_21
  assign D13 = y ? demultiplexer_1_out13 : 8'bz;  // Controlled_Buffer controlled_buffer_22
  assign D11 = y ? demultiplexer_1_out11 : 8'bz;  // Controlled_Buffer controlled_buffer_23
  assign D9 = y ? demultiplexer_1_out9 : 8'bz;  // Controlled_Buffer controlled_buffer_24
  assign D10 = y ? demultiplexer_1_out10 : 8'bz;  // Controlled_Buffer controlled_buffer_25
  Multiplexer #(.select(5), .width(8)) multiplexer_4 (
    .in0(O0), .in1(O1), .in2(O2), .in3(O3), .in4(O4), .in5(O5), .in6(O6), .in7(O7), .in8(O8), .in9(O9),
    .in10(O10), .in11(O11), .in12(O12), .in13(O13), .in14(O14), .in15(O15), .in16(O16), .in17(O17),
    .in18(O18), .in19(O19), .in20(O20), .in21(O21), .in22(O22), .in23(O23), .in24(O24), .in25(O25),
    .in26(O26), .in27(O27), .in28(O28), .in29(O29), .in30(O30), .in31(O31), .out(multiplexer_4_out),
    .sel(InputSelect[4:0]));  // open: en
  Multiplexer #(.select(5), .width(8)) multiplexer_5 (
    .in0(O0), .in1(O1), .in2(O2), .in3(O3), .in4(O4), .in5(O5), .in6(O6), .in7(O7), .in8(O8), .in9(O9),
    .in10(O10), .in11(O11), .in12(O12), .in13(O13), .in14(O14), .in15(O15), .in16(O16), .in17(O17),
    .in18(O18), .in19(O19), .in20(O20), .in21(O21), .in22(O22), .in23(O23), .in24(O24), .in25(O25),
    .in26(O26), .in27(O27), .in28(O28), .in29(O29), .in30(O30), .in31(O31), .out(RAM_output),
    .sel(OutputSelect));  // open: en
  assign D7 = y ? demultiplexer_1_out7 : 8'bz;  // Controlled_Buffer controlled_buffer_26
  assign D8 = y ? demultiplexer_1_out8 : 8'bz;  // Controlled_Buffer controlled_buffer_27
  assign D5 = y ? demultiplexer_1_out5 : 8'bz;  // Controlled_Buffer controlled_buffer_28
  assign D6 = y ? demultiplexer_1_out6 : 8'bz;  // Controlled_Buffer controlled_buffer_29
  assign D3 = y ? demultiplexer_1_out3 : 8'bz;  // Controlled_Buffer controlled_buffer_30
  assign D4 = y ? demultiplexer_1_out4 : 8'bz;  // Controlled_Buffer controlled_buffer_31
  assign D1 = y ? demultiplexer_1_out1 : 8'bz;  // Controlled_Buffer controlled_buffer_32
  assign D2 = y ? demultiplexer_1_out2 : 8'bz;  // Controlled_Buffer controlled_buffer_33
  assign D0 = y ? demultiplexer_1_out0 : 8'bz;  // Controlled_Buffer controlled_buffer_34

  // Other names for the same wires on the sheet: Select[4:0] = InputSelect[4:0]
endmodule
