// Logisim project STATE_MACHINE.circ as structural Verilog: 2 circuits, main circuit main
// 3
module main (
);
endmodule

module State_Machine (
  input  [15:0] in_1,
  input  in_2,
  input  in_3,
  output [4:0] out_4
);

  wire _01101, _01110, and_45_out, and_46_out, and_47_out, and_48_out, and_49_out, and_50_out, and_51_out,
       and_52_out, and_53_out, and_54_out, and_55_out, and_56_out, and_57_out, CS0, CS1, CS2, CS3, CS4, CS5,
       CS6, CS7, CS8, CS9, CS10, CS11, CS12, CS13, CS14, CS15, CS16, CS17, CS18, CS19, CS20, D0, D1, D2, D3,
       D4, HALT, IN0, IN1, IN2, IN3, IN4, IN5, IN6, IN7, IN8, IN9, IN10, IN11, IN12, IN13, IN15, IN16, JUMP,
       MOVE, or_1_out, or_2_out, or_4_out, or_6_out, or_7_out, or_8_out, or_10_out, or_12_out, or_14_out,
       or_15_out, SI, SM, SR, STORE;

  and and_1 (IN0, ~in_1[15], ~in_1[14], ~in_1[13], ~in_1[12], ~in_1[11]);  // AND_Gate
  and and_2 (IN12, in_1[15], ~in_1[14], ~in_1[13], ~in_1[12], ~in_1[11]);  // AND_Gate
  and and_3 (STORE, in_1[15], ~in_1[14], ~in_1[13], ~in_1[12], in_1[11]);  // AND_Gate
  and and_4 (MOVE, in_1[15], ~in_1[14], ~in_1[13], in_1[12], ~in_1[11]);  // AND_Gate
  and and_5 (JUMP, ~in_1[15], in_1[14], in_1[13], in_1[12], in_1[11]);  // AND_Gate
  and and_6 (HALT, in_1[15], in_1[14], in_1[13], in_1[12], in_1[11]);
  and and_7 (IN10, ~in_1[15], ~in_1[14], ~in_1[13], in_1[12], in_1[11]);  // AND_Gate
  and and_8 (_01101, ~in_1[15], in_1[14], in_1[13], ~in_1[12], in_1[11]);  // AND_Gate
  and and_9 (_01110, ~in_1[15], in_1[14], in_1[13], in_1[12], ~in_1[11]);  // AND_Gate
  and and_10 (SR, ~in_1[10], ~in_1[9]);  // AND_Gate
  and and_11 (SI, in_1[10], ~in_1[9]);  // AND_Gate
  and and_12 (SM, ~in_1[10], in_1[9]);  // AND_Gate
  and and_13 (IN1, JUMP, ~IN0);  // AND_Gate
  and and_14 (IN2, ~in_1[15], ~_01101, ~_01110, SR, ~IN0, ~IN1);  // AND_Gate
  and and_15 (IN3, ~in_1[15], ~_01101, ~_01110, ~SR, ~IN0, ~IN1, ~IN2);  // AND_Gate
  and and_16 (IN4, IN12, SR, ~IN0, ~IN1, ~IN2, ~IN3);  // AND_Gate
  and and_17 (IN5, IN12, SI, ~IN0, ~IN1, ~IN2, ~IN3, ~IN4);  // AND_Gate
  and and_18 (IN6, IN12, SM, ~IN0, ~IN1, ~IN2, ~IN3, ~IN4, ~IN5);  // AND_Gate
  D_Flip_Flop d_ff_1 (.clk(in_2), .D(D0), .Q(out_4[0]), .reset(in_3));  // open: Qn, preset, en
  D_Flip_Flop d_ff_2 (.clk(in_2), .D(D1), .Q(out_4[1]), .reset(in_3));  // open: Qn, preset, en
  D_Flip_Flop d_ff_3 (.clk(in_2), .D(D2), .Q(out_4[2]), .reset(in_3));  // open: Qn, preset, en
  D_Flip_Flop d_ff_4 (.clk(in_2), .D(D3), .Q(out_4[3]), .reset(in_3));  // open: Qn, preset, en
  D_Flip_Flop d_ff_5 (.clk(in_2), .D(D4), .Q(out_4[4]), .reset(in_3));  // open: Qn, preset, en
  or or_1 (or_1_out, MOVE, STORE);
  and and_19 (IN7, or_1_out, ~IN0, ~IN1, ~IN2, ~IN3, ~IN4, ~IN5, ~IN6);  // AND_Gate
  and and_20 (IN8, HALT, ~IN0, ~IN1, ~IN2, ~IN3, ~IN4, ~IN5, ~IN6, ~IN7);  // AND_Gate
  and and_21 (IN9, ~IN8, ~IN7, ~IN6, ~IN5, ~IN4, ~IN3, ~IN2, ~IN1, ~IN0);  // AND_Gate
  not not_1 (IN11, IN10);
  not not_2 (IN13, IN12);
  and and_22 (IN15, STORE, ~IN12);  // AND_Gate
  and and_23 (IN16, MOVE, ~IN15, ~IN12);  // AND_Gate
  and and_24 (CS0, ~out_4[4], ~out_4[3], ~out_4[2], ~out_4[1], ~out_4[0]);  // AND_Gate
  and and_25 (CS1, ~out_4[4], ~out_4[3], ~out_4[2], ~out_4[1], out_4[0]);  // AND_Gate
  and and_26 (CS2, ~out_4[4], ~out_4[3], ~out_4[2], out_4[1], ~out_4[0]);  // AND_Gate
  and and_27 (CS3, ~out_4[4], ~out_4[3], ~out_4[2], out_4[1], out_4[0]);  // AND_Gate
  and and_28 (CS4, ~out_4[4], ~out_4[3], out_4[2], ~out_4[1], ~out_4[0]);  // AND_Gate
  and and_29 (CS5, ~out_4[4], ~out_4[3], out_4[2], ~out_4[1], out_4[0]);  // AND_Gate
  and and_30 (CS6, ~out_4[4], ~out_4[3], out_4[2], out_4[1], ~out_4[0]);  // AND_Gate
  and and_31 (CS7, ~out_4[4], ~out_4[3], out_4[2], out_4[1], out_4[0]);  // AND_Gate
  and and_32 (CS8, ~out_4[4], out_4[3], ~out_4[2], ~out_4[1], ~out_4[0]);  // AND_Gate
  and and_33 (CS9, ~out_4[4], out_4[3], ~out_4[2], ~out_4[1], out_4[0]);  // AND_Gate
  and and_34 (CS10, ~out_4[4], out_4[3], ~out_4[2], out_4[1], ~out_4[0]);  // AND_Gate
  and and_35 (CS11, ~out_4[4], out_4[3], ~out_4[2], out_4[1], out_4[0]);  // AND_Gate
  and and_36 (CS12, ~out_4[4], out_4[3], out_4[2], ~out_4[1], ~out_4[0]);  // AND_Gate
  and and_37 (CS13, ~out_4[4], out_4[3], out_4[2], ~out_4[1], out_4[0]);  // AND_Gate
  and and_38 (CS14, ~out_4[4], out_4[3], out_4[2], out_4[1], ~out_4[0]);  // AND_Gate
  and and_39 (CS15, ~out_4[4], out_4[3], out_4[2], out_4[1], out_4[0]);  // AND_Gate
  and and_40 (CS16, out_4[4], ~out_4[3], ~out_4[2], ~out_4[1], ~out_4[0]);  // AND_Gate
  and and_41 (CS17, out_4[4], ~out_4[3], ~out_4[2], ~out_4[1], out_4[0]);  // AND_Gate
  and and_42 (CS18, out_4[4], ~out_4[3], ~out_4[2], out_4[1], ~out_4[0]);  // AND_Gate
  and and_43 (CS19, out_4[4], ~out_4[3], ~out_4[2], out_4[1], out_4[0]);  // AND_Gate
  and and_44 (CS20, out_4[4], ~out_4[3], out_4[2], ~out_4[1], ~out_4[0]);  // AND_Gate
  or or_2 (or_2_out, IN12, IN13);
  and and_45 (and_45_out, CS6, or_2_out);
  or or_3 (D0, CS19, CS18, CS16, CS15, CS14, CS12, CS11, CS10, CS8, CS7, CS5, CS0, and_45_out, and_47_out, and_48_out, and_51_out);
  or or_4 (or_4_out, IN12, IN15);
  and and_46 (and_46_out, CS9, or_4_out);
  or or_5 (D1, CS19, CS17, CS14, CS13, CS1, and_46_out, and_49_out, and_50_out);
  or or_6 (or_6_out, IN10, IN11);
  or or_7 (or_7_out, IN0, IN2, IN4, IN8, IN9);
  and and_47 (and_47_out, CS4, or_6_out);
  and and_48 (and_48_out, CS2, or_7_out);
  or or_8 (or_8_out, IN2, IN4, IN5, IN8, IN9);
  and and_49 (and_49_out, CS2, or_8_out);
  and and_50 (and_50_out, CS6, IN13);
  and and_51 (and_51_out, CS9, IN15);
  and and_52 (and_52_out, CS9, IN16);
  or or_9 (D2, CS14, CS13, CS12, CS20, CS3, and_52_out, and_55_out, and_56_out);
  or or_10 (or_10_out, IN6, IN7);
  and and_53 (and_53_out, or_10_out, CS2);
  or or_11 (D3, CS14, CS13, CS12, CS8, and_53_out, and_57_out);
  or or_12 (or_12_out, IN1, IN3, IN8, IN9);
  and and_54 (and_54_out, or_12_out, CS2);
  or or_13 (D4, CS18, CS17, CS16, and_54_out);
  or or_14 (or_14_out, IN3, IN4, IN5);
  and and_55 (and_55_out, IN10, CS4);
  and and_56 (and_56_out, CS2, or_14_out);
  or or_15 (or_15_out, IN12, IN15, IN16);
  and and_57 (and_57_out, CS9, or_15_out);

  // Other names for the same wires on the sheet: clock = in_2; _9 = in_1[9]; _10 = in_1[10]; _11 = in_1[11];
  //   _12 = in_1[12]; _13 = in_1[13]; _14 = in_1[14]; _15 = in_1[15]; IN14 = IN12; LOAD = IN12; MUL = IN10; NOP = IN0;
  //   Q0 = out_4[0]; Q1 = out_4[1]; Q2 = out_4[2]; Q3 = out_4[3]; Q4 = out_4[4]; reset = in_3

  // Notes on the sheet:
  //   Input (IR)
  //   Opcode & Source Addressing Mode Check
  //   Output (State)
  //   Clock
  //   Conditions Check
  //   Reset
  //   Next States
  //   Current States
  //   Output Equations
endmodule
