// Logisim project latch.circ as structural Verilog: 2 circuits, main circuit alu_latch
module main (
  input  in_1,
  input  in_2,
  input  in_3,
  input  in_4,
  input  [15:0] in_5,
  input  [2:0] in_6,
  output [7:0] out_7,
  output [2:0] out_8
);

  wire clock_1_out;

  Clock clock_1 (.out(clock_1_out));
  alu_latch alu_latch_1 (
    .clk(clock_1_out), .store_hight(in_1), .store_low(in_2), .reset(in_3), .grap(in_4), .in_6(in_5),
    .flags(in_6), .out(out_7), .flags_out(out_8));
endmodule

module alu_latch (
  input  clk,
  input  store_hight,
  input  store_low,
  input  reset,
  input  grap,
  input  [15:0] in_6,
  input  [2:0] flags,
  output [7:0] out,
  output [2:0] flags_out
);

  wire not_1_out, or_1_out, or_2_out;
  wire [15:0] register_1_q;

  Register #(.width(16)) register_1 (.D(in_6), .en(grap), .Q(register_1_q), .clk(clk), .clr(reset));
  Multiplexer #(.width(8)) multiplexer_1 (
    .in0(register_1_q[7:0]), .in1(register_1_q[15:8]), .out(out), .sel(or_1_out), .en(or_2_out));
  or or_1 (or_1_out, not_1_out, store_hight);
  not not_1 (not_1_out, store_low);
  or or_2 (or_2_out, store_low, store_hight);
  assign flags_out = grap ? flags : 3'bz;  // Controlled_Buffer controlled_buffer_1

  // Other names for the same wires on the sheet: alu_result[15:0] = in_6; st_high = store_hight; st_low = store_low

  // Notes on the sheet:
  //   flags_out: pull=up
  //   out: pull=up
  //   alu result
endmodule
